# Fritzing sketch schema_circuit (saved by Fritzing 0.9.3b)
breadboards: 1

parts:
  Part1 = Arduino Uno (Rev3)
  M1 = fc-51 [package=THT]
  M2 = fc-51 [package=THT]
  M3 = fc-51 [package=THT]
  M4 = fc-51 [package=THT]
  M5 = fc-51 [package=THT]
  M6 = fc-51 [package=THT]
  J1 = Basic Servo
  LED1 = LED - 5mm [color="Yellow (595nm)" package="5 mm [THT]"]
  LED2 = LED - 5mm [color="Yellow (595nm)" package="5 mm [THT]"]
  LED3 = LED - 5mm [color="Yellow (595nm)" package="5 mm [THT]"]
  LED4 = LED - 5mm [color="Yellow (595nm)" package="5 mm [THT]"]
  R1 = Resistor [tolerance=±5% resistance=10 package="2512 [SMD]"]  # not connected
  R3 = Resistor [tolerance=±5% resistance=10 package="2512 [SMD]"]  # not connected
  R4 = Resistor [tolerance=±5% resistance=10 package="2512 [SMD]"]  # not connected
  R5 = Resistor [tolerance=±5% resistance=10 package="2512 [SMD]"]  # not connected
  Part2 = LCD1602-I2C

nets:
  N1: Part1.D8, M6.pin1
  N2: Part1.D9_PWM, LED1.cathode
  N3: Part1.D10_PWM/SS, LED2.cathode
  N4: Part1.D11_PWM/MOSI, LED3.cathode
  N5: Part1.D12/MISO, LED4.cathode
  N6: Part1.A4/SDA, Part2.SDA
  N7: Part1.A5/SCL, Part2.SCL
  N8: Part1.D2, M3.pin1
  N9: Part1.D3_PWM, J1.pulse
  N10: Part1.D4, M2.pin1
  N11: Part1.D5_PWM, M1.pin1
  N12: Part1.D6_PWM, M4.pin1
  N13: Part1.D7, M5.pin1
  N14: Part1.ioref, Part2.VCC
  5V: Part1.5V, M1.pin3, M2.pin3, M3.pin3, J1.vcc
  GND: Part1.GND, M2.pin2, M3.pin2, J1.gnd, Part2.GND

custom parts:
  LCD1602-I2C: A standard character display, usually with 2x16 characters. Comes in many colors with LCM1602 IIC attached.
